// Logisim project trabalhoCircuitos.circ as structural Verilog
module main (
  input  in_1,
  input  JOGAR,
  input  JOGADOR_0,
  input  in_4,
  input  in_5,
  input  in_6,
  input  in_7,
  input  in_8,
  input  JOGADOR_1,
  input  in_10,
  output A___B,
  output A___B_2,
  output A___B_3
);

  wire constante_1_out_1, constante_1_out_2, constante_1_out_3, constante_1_out_4, finaldisplay_1_out_5,
       finaldisplay_1_out_6, finaldisplay_1_out_7, finaldisplay_1_out_8, finaldisplay_1_out_9,
       finaldisplay_1_out_10, finaldisplay_1_out_11, finaldisplay_1_out_12, finaldisplay_2_out_5,
       finaldisplay_2_out_6, finaldisplay_2_out_7, finaldisplay_2_out_8, finaldisplay_2_out_9,
       finaldisplay_2_out_10, finaldisplay_2_out_11, finaldisplay_2_out_12, multiplexador4bits_1_out_10,
       multiplexador4bits_1_out_11, multiplexador4bits_1_out_12, multiplexador4bits_1_out_13;

  finalDisplay finaldisplay_1 (
    .in_1(JOGADOR_0), .in_2(in_4), .in_3(in_5), .in_4(in_6), .out_5(finaldisplay_1_out_5),
    .out_6(finaldisplay_1_out_6), .out_7(finaldisplay_1_out_7), .out_8(finaldisplay_1_out_8),
    .out_9(finaldisplay_1_out_9), .out_10(finaldisplay_1_out_10), .out_11(finaldisplay_1_out_11),
    .out_12(finaldisplay_1_out_12));
  finalDisplay finaldisplay_2 (
    .in_1(in_7), .in_2(in_8), .in_3(JOGADOR_1), .in_4(in_10), .out_5(finaldisplay_2_out_5),
    .out_6(finaldisplay_2_out_6), .out_7(finaldisplay_2_out_7), .out_8(finaldisplay_2_out_8),
    .out_9(finaldisplay_2_out_9), .out_10(finaldisplay_2_out_10), .out_11(finaldisplay_2_out_11),
    .out_12(finaldisplay_2_out_12));
  _7_Segment_Display u_7_segment_display_1 (
    .g(finaldisplay_2_out_8), .f(finaldisplay_2_out_7), .a(finaldisplay_2_out_6), .b(finaldisplay_2_out_5),
    .e(finaldisplay_2_out_9), .d(finaldisplay_2_out_10), .c(finaldisplay_2_out_11), .dp(finaldisplay_2_out_12));
  _7_Segment_Display u_7_segment_display_2 (
    .g(finaldisplay_1_out_8), .f(finaldisplay_1_out_7), .a(finaldisplay_1_out_6), .b(finaldisplay_1_out_5),
    .e(finaldisplay_1_out_9), .d(finaldisplay_1_out_10), .c(finaldisplay_1_out_11), .dp(finaldisplay_1_out_12));
  multiplexador4Bits multiplexador4bits_1 (
    .in_1(in_1), .out_10(multiplexador4bits_1_out_10), .out_11(multiplexador4bits_1_out_11),
    .out_12(multiplexador4bits_1_out_12), .out_13(multiplexador4bits_1_out_13), .in_2(JOGADOR_0),
    .in_3(in_4), .in_4(in_5), .in_5(in_6), .in_6(in_7), .in_7(in_8), .in_8(JOGADOR_1), .in_9(in_10));
  constante constante_1 (
    .out_1(constante_1_out_1), .out_2(constante_1_out_2), .out_3(constante_1_out_3), .out_4(constante_1_out_4));
  COMPARADOR_V1 comparador_v1_1 (
    .in_2(multiplexador4bits_1_out_10), .in_3(multiplexador4bits_1_out_11),
    .in_4(multiplexador4bits_1_out_12), .in_5(multiplexador4bits_1_out_13), .in_6(constante_1_out_4),
    .in_7(constante_1_out_3), .in_8(constante_1_out_2), .in_9(constante_1_out_1), .in_1(JOGAR),
    .out_10(A___B), .A___B(A___B_2), .A___B_2(A___B_3));

  // Notes on the sheet:
  //   ESCOLHA DO
  //   JOGADOR 1
  //   ESCOLHA DO
  //   JOGADOR 0
  //   JOGADOR DA VEZ (A)
  //   NÚMERO "SECRETO" (B)
endmodule

module Porta_XOR (
  input  in_1,
  input  in_2,
  output out_3
);

  wire and_1_out, and_2_out, not_1_out, not_2_out, or_1_out;

  not not_1 (not_1_out, in_1);
  not not_2 (not_2_out, in_2);
  and and_1 (and_1_out, in_1, in_2);
  and and_2 (and_2_out, not_1_out, not_2_out);
  or or_1 (or_1_out, and_1_out, and_2_out);
  not not_3 (out_3, or_1_out);
endmodule

// XNOR
module Porta_XNOR (
  input  in_1,
  input  in_2,
  output out_3
);

  wire porta_xor_1_out_3;

  Porta_XOR porta_xor_1 (.in_1(in_1), .in_2(in_2), .out_3(porta_xor_1_out_3));
  not not_1 (out_3, porta_xor_1_out_3);
endmodule

// COMPARA
module COMPARADOR_V1 (
  input  in_1,
  input  in_2,
  input  in_3,
  input  in_4,
  input  in_5,
  input  in_6,
  input  in_7,
  input  in_8,
  input  in_9,
  output out_10,
  output A___B,
  output A___B_2
);

  wire and_1_out, and_2_out, and_3_out, and_4_out, and_5_out, not_1_out, not_2_out, not_3_out, not_4_out,
       not_5_out, or_1_out, or_2_out, porta_xnor_1_out_3, porta_xnor_2_out_3, porta_xnor_3_out_3,
       porta_xnor_4_out_3;

  Porta_XNOR porta_xnor_1 (.in_1(in_2), .out_3(porta_xnor_1_out_3), .in_2(in_9));
  Porta_XNOR porta_xnor_2 (.in_1(in_3), .out_3(porta_xnor_2_out_3), .in_2(in_8));
  Porta_XNOR porta_xnor_3 (.in_1(in_4), .out_3(porta_xnor_3_out_3), .in_2(in_7));
  Porta_XNOR porta_xnor_4 (.in_1(in_5), .out_3(porta_xnor_4_out_3), .in_2(in_6));
  not not_1 (not_1_out, in_9);
  not not_2 (not_2_out, in_8);
  not not_3 (not_3_out, in_7);
  not not_4 (not_4_out, in_6);
  and and_1 (and_1_out, in_2, not_1_out);
  and and_2 (and_2_out, in_3, porta_xnor_1_out_3, not_2_out);
  and and_3 (and_3_out, in_4, porta_xnor_1_out_3, porta_xnor_2_out_3, not_3_out);
  and and_4 (and_4_out, in_5, porta_xnor_1_out_3, porta_xnor_2_out_3, porta_xnor_3_out_3, not_4_out);
  and and_5 (and_5_out, porta_xnor_1_out_3, porta_xnor_2_out_3, porta_xnor_3_out_3, porta_xnor_4_out_3);
  or or_1 (or_1_out, and_1_out, and_2_out, and_3_out, and_4_out);
  or or_2 (or_2_out, and_5_out, or_1_out);
  not not_5 (not_5_out, or_2_out);
  and and_6 (out_10, in_1, and_5_out);
  and and_7 (A___B, in_1, or_1_out);
  and and_8 (A___B_2, in_1, not_5_out);
endmodule

module multiplexador1Bit (
  input  A,
  input  B,
  output out_3
);

  wire and_1_out, and_2_out, undriven;

  and and_1 (and_1_out, A, ~undriven);  // AND_Gate
  and and_2 (and_2_out, undriven, B);
  or or_1 (out_3, and_1_out, and_2_out);
endmodule

// MULTIPLEX
module multiplexador4Bits (
  input  in_1,
  input  in_2,
  input  in_3,
  input  in_4,
  input  in_5,
  input  in_6,
  input  in_7,
  input  in_8,
  input  in_9,
  output out_10,
  output out_11,
  output out_12,
  output out_13
);

  wire and_1_out, and_2_out, and_3_out, and_4_out, and_5_out, and_6_out, and_7_out, and_8_out;

  and and_1 (and_1_out, in_2, ~in_1);  // AND_Gate
  and and_2 (and_2_out, in_1, in_6);
  and and_3 (and_3_out, in_3, ~in_1);  // AND_Gate
  and and_4 (and_4_out, in_1, in_7);
  and and_5 (and_5_out, in_4, ~in_1);  // AND_Gate
  and and_6 (and_6_out, in_1, in_8);
  and and_7 (and_7_out, in_5, ~in_1);  // AND_Gate
  and and_8 (and_8_out, in_1, in_9);
  or or_1 (out_10, and_1_out, and_2_out);
  or or_2 (out_11, and_3_out, and_4_out);
  or or_3 (out_12, and_5_out, and_6_out);
  or or_4 (out_13, and_7_out, and_8_out);
endmodule

// a
module displayA (
  input  in_1,
  input  in_2,
  input  in_3,
  input  in_4,
  output out_5
);

  wire and_1_out, and_2_out, and_3_out, and_4_out, and_5_out;

  and and_1 (and_1_out, ~in_1, in_2, ~in_3);  // AND_Gate
  and and_2 (and_2_out, in_1, in_4);
  and and_3 (and_3_out, ~in_2, in_3);  // AND_Gate
  and and_4 (and_4_out, in_1, ~in_2);  // AND_Gate
  and and_5 (and_5_out, in_3, ~in_4);  // AND_Gate
  or or_1 (out_5, and_1_out, and_2_out, and_3_out, and_4_out, and_5_out);
endmodule

// b
module displayB (
  input  in_1,
  input  in_2,
  input  in_3,
  input  in_4,
  output out_5
);

  wire and_1_out, and_2_out, and_3_out, and_4_out, and_5_out;

  and and_1 (and_1_out, ~in_1, in_2, ~in_3);  // AND_Gate
  and and_2 (and_2_out, in_2, ~in_4);  // AND_Gate
  and and_3 (and_3_out, ~in_3, ~in_4);  // AND_Gate
  and and_4 (and_4_out, in_1, ~in_2);  // AND_Gate
  and and_5 (and_5_out, in_1, in_3);
  or or_1 (out_5, and_1_out, and_2_out, and_3_out, and_4_out, and_5_out);
endmodule

// c
module displayC (
  input  in_1,
  input  in_2,
  input  in_3,
  input  in_4,
  output out_5
);

  wire and_1_out, and_2_out, and_3_out, and_4_out, and_5_out, and_6_out;

  and and_1 (and_1_out, ~in_1, in_2, in_4);  // AND_Gate
  and and_2 (and_2_out, in_1, ~in_2, ~in_3);  // AND_Gate
  and and_3 (and_3_out, in_1, ~in_4);  // AND_Gate
  and and_4 (and_4_out, ~in_2, ~in_4);  // AND_Gate
  and and_5 (and_5_out, ~in_1, in_3);  // AND_Gate
  and and_6 (and_6_out, in_2, in_3);
  or or_1 (out_5, and_1_out, and_2_out, and_3_out, and_4_out, and_5_out, and_6_out);
endmodule

// d
module displayD (
  input  in_1,
  input  in_2,
  input  in_3,
  input  in_4,
  output out_5
);

  wire and_1_out, and_2_out, and_3_out, and_4_out, and_5_out;

  and and_1 (and_1_out, ~in_1, ~in_3, ~in_4);  // AND_Gate
  and and_2 (and_2_out, in_1, ~in_3, in_4);  // AND_Gate
  and and_3 (and_3_out, ~in_1, in_3, in_4);  // AND_Gate
  and and_4 (and_4_out, ~in_2, ~in_3);  // AND_Gate
  and and_5 (and_5_out, ~in_2, ~in_4);  // AND_Gate
  or or_1 (out_5, and_1_out, and_2_out, and_3_out, and_4_out, and_5_out);
endmodule

// f
module displayF (
  input  in_1,
  input  in_2,
  input  in_3,
  input  in_4,
  output out_5
);

  wire and_1_out, and_2_out, and_3_out, and_4_out, and_5_out;

  and and_1 (and_1_out, ~in_1, ~in_3);  // AND_Gate
  and and_2 (and_2_out, ~in_1, in_4);  // AND_Gate
  and and_3 (and_3_out, ~in_3, in_4);  // AND_Gate
  and and_4 (and_4_out, ~in_1, in_2);  // AND_Gate
  and and_5 (and_5_out, in_1, ~in_2);  // AND_Gate
  or or_1 (out_5, and_1_out, and_2_out, and_3_out, and_4_out, and_5_out);
endmodule

// g
module displayG (
  input  in_1,
  input  in_2,
  input  in_3,
  input  in_4,
  output out_5
);

  wire and_1_out, and_2_out, and_3_out, and_4_out, and_5_out, and_6_out;

  and and_1 (and_1_out, ~in_1, ~in_2, ~in_4);  // AND_Gate
  and and_2 (and_2_out, ~in_1, ~in_2, in_3);  // AND_Gate
  and and_3 (and_3_out, in_2, ~in_3, in_4);  // AND_Gate
  and and_4 (and_4_out, in_2, in_3, ~in_4);  // AND_Gate
  and and_5 (and_5_out, in_1, ~in_2, in_4);  // AND_Gate
  and and_6 (and_6_out, in_1, ~in_3);  // AND_Gate
  or or_1 (out_5, and_1_out, and_2_out, and_3_out, and_4_out, and_5_out, and_6_out);
endmodule

// h
module displayH (
  input  in_1,
  input  in_2,
  input  in_3,
  input  in_4,
  output out_5
);

  wire and_1_out, and_2_out, and_3_out, and_4_out;

  and and_1 (and_1_out, ~in_2, ~in_4);  // AND_Gate
  and and_2 (and_2_out, in_1, in_3);
  and and_3 (and_3_out, in_1, in_2);
  and and_4 (and_4_out, in_3, ~in_4);  // AND_Gate
  or or_1 (out_5, and_1_out, and_2_out, and_3_out, and_4_out);
endmodule

// e
module displayE (
  input  in_1,
  input  in_2,
  input  in_3,
  input  in_4,
  output out_5
);

  wire and_1_out;

  and and_1 (and_1_out, in_1, ~in_1);  // AND_Gate
  and and_2 (out_5, in_4, in_3, in_2, and_1_out);
endmodule

// DISPLAY
module finalDisplay (
  input  in_1,
  input  in_2,
  input  in_3,
  input  in_4,
  output out_5,
  output out_6,
  output out_7,
  output out_8,
  output out_9,
  output out_10,
  output out_11,
  output out_12
);

  displayD displayd_1 (.in_1(in_1), .in_2(in_2), .in_3(in_3), .in_4(in_4), .out_5(out_5));
  displayC displayc_1 (.in_1(in_1), .in_2(in_2), .in_3(in_3), .in_4(in_4), .out_5(out_6));
  displayB displayb_1 (.in_1(in_1), .in_2(in_2), .in_3(in_3), .in_4(in_4), .out_5(out_7));
  displayA displaya_1 (.in_1(in_1), .in_2(in_2), .in_3(in_3), .in_4(in_4), .out_5(out_8));
  displayH displayh_1 (.in_1(in_1), .in_2(in_2), .in_3(in_3), .in_4(in_4), .out_5(out_9));
  displayG displayg_1 (.in_1(in_1), .in_2(in_2), .in_3(in_3), .in_4(in_4), .out_5(out_10));
  displayF displayf_1 (.in_1(in_1), .in_2(in_2), .in_3(in_3), .in_4(in_4), .out_5(out_11));
  displayE displaye_1 (.in_1(in_1), .in_2(in_2), .in_3(in_3), .in_4(in_4), .out_5(out_12));
endmodule

// ?
module constante (
  output out_1,
  output out_2,
  output out_3,
  output out_4
);


  assign out_1 = 1'b0;
  assign out_2 = 1'b1;
  assign out_3 = 1'b1;
  assign out_4 = 1'b0;
endmodule
